// Logisim project LadnerFischerAdderBasic.circ as structural Verilog: 1 circuit, main circuit main
module main (
  input  A6,
  input  A5,
  input  A4,
  input  A3,
  input  A2,
  input  A1,
  input  A0,
  input  A6_2,
  input  A5_2,
  input  A4_2,
  input  A3_2,
  input  A2_2,
  input  A1_2,
  input  A0_2,
  input  B6,
  input  B5,
  input  B4,
  input  B3,
  input  B2,
  input  B1,
  input  B0,
  input  B6_2,
  input  B5_2,
  input  B4_2,
  input  B3_2,
  input  B2_2,
  input  B1_2,
  input  B0_2
);

  wire and_1_out, and_2_out, and_3_out, and_4_out, and_5_out, and_6_out, and_7_out, and_8_out, and_9_out,
       and_10_out, and_11_out, and_12_out, and_13_out, and_14_out, and_15_out, and_16_out, and_17_out,
       and_18_out, and_19_out, and_20_out, and_21_out, and_22_out, and_23_out, and_24_out, and_25_out,
       and_26_out, and_27_out, and_28_out, and_29_out, and_30_out, and_31_out, and_32_out, and_33_out,
       and_34_out, and_35_out, and_36_out, and_37_out, and_38_out, and_39_out, and_40_out, and_41_out,
       and_42_out, and_44_out, and_45_out, and_46_out, and_47_out, and_48_out, and_49_out, and_51_out,
       and_52_out, and_53_out, and_55_out, and_56_out, and_57_out, and_58_out, and_59_out, and_60_out,
       and_61_out, and_62_out, and_63_out, and_64_out, and_65_out, and_66_out, and_68_out, and_69_out,
       and_70_out, or_1_out, or_2_out, or_3_out, or_4_out, or_5_out, or_6_out, or_7_out, or_8_out, or_9_out,
       or_10_out, or_11_out, or_12_out, or_13_out, or_14_out, or_15_out, or_16_out, or_17_out, or_18_out,
       or_19_out, or_20_out, or_21_out, or_22_out, or_23_out, or_24_out, or_25_out, or_26_out, or_27_out,
       or_28_out, or_29_out, or_30_out, or_31_out, or_32_out, or_33_out, or_34_out, or_35_out, or_36_out,
       or_37_out, or_38_out, or_39_out, or_40_out, or_41_out, or_42_out, xor_1_out, xor_2_out, xor_3_out,
       xor_4_out, xor_5_out, xor_6_out, xor_7_out, xor_8_out, xor_9_out, xor_10_out, xor_11_out, xor_12_out,
       xor_13_out;

  and and_1 (and_1_out, or_18_out, and_9_out);
  or or_1 (or_1_out, or_3_out, and_1_out);
  buf xor_1 (xor_1_out, or_4_out);  // XOR_Gate
  LED led_1 (.in(xor_1_out));
  and and_2 (and_2_out, A6, B6);
  and and_3 (and_3_out, ~and_2_out, or_5_out);  // AND_Gate
  and and_4 (and_4_out, and_7_out, or_5_out);
  or or_2 (or_2_out, and_2_out, and_4_out);
  and and_5 (and_5_out, or_10_out, and_8_out);
  or or_3 (or_3_out, or_2_out, and_5_out);
  and and_6 (and_6_out, and_9_out, and_31_out);
  or or_4 (or_4_out, or_1_out, and_6_out);
  or or_5 (or_5_out, A6, B6);
  and and_7 (and_7_out, A5, B5);
  and and_8 (and_8_out, or_5_out, or_9_out);
  and and_9 (and_9_out, and_8_out, and_20_out);
  or or_6 (or_6_out, and_7_out, and_12_out);
  and and_10 (and_10_out, or_18_out, and_13_out);
  or or_7 (or_7_out, or_6_out, and_10_out);
  or or_8 (or_8_out, or_7_out, and_14_out);
  xor xor_2 (xor_2_out, and_3_out, or_8_out);
  LED led_2 (.in(xor_2_out));
  or or_9 (or_9_out, A5, B5);
  and and_11 (and_11_out, ~and_7_out, or_9_out);  // AND_Gate
  and and_12 (and_12_out, or_10_out, or_9_out);
  and and_13 (and_13_out, or_9_out, and_20_out);
  and and_14 (and_14_out, and_13_out, and_31_out);
  and and_15 (and_15_out, A4, B4);
  and and_16 (and_16_out, ~and_15_out, or_13_out);  // AND_Gate
  and and_17 (and_17_out, and_19_out, or_13_out);
  or or_10 (or_10_out, and_15_out, and_17_out);
  and and_18 (and_18_out, or_18_out, and_20_out);
  or or_11 (or_11_out, or_10_out, and_18_out);
  or or_12 (or_12_out, or_11_out, and_21_out);
  xor xor_3 (xor_3_out, and_11_out, or_12_out);
  LED led_3 (.in(xor_3_out));
  or or_13 (or_13_out, A4, B4);
  and and_19 (and_19_out, A3, B3);
  and and_20 (and_20_out, or_13_out, or_15_out);
  and and_21 (and_21_out, and_20_out, and_31_out);
  or or_14 (or_14_out, and_19_out, and_23_out);
  or or_15 (or_15_out, A3, B3);
  and and_22 (and_22_out, ~and_19_out, or_15_out);  // AND_Gate
  and and_23 (and_23_out, or_18_out, or_15_out);
  and and_24 (and_24_out, or_15_out, and_31_out);
  or or_16 (or_16_out, or_14_out, and_24_out);
  xor xor_4 (xor_4_out, and_16_out, or_16_out);
  LED led_4 (.in(xor_4_out));
  and and_25 (and_25_out, A2, B2);
  and and_26 (and_26_out, ~and_25_out, or_20_out);  // AND_Gate
  and and_27 (and_27_out, and_29_out, or_20_out);
  or or_17 (or_17_out, and_25_out, and_27_out);
  and and_28 (and_28_out, or_24_out, and_30_out);
  or or_18 (or_18_out, or_17_out, and_28_out);
  or or_19 (or_19_out, or_18_out, and_31_out);
  xor xor_5 (xor_5_out, and_22_out, or_19_out);
  LED led_5 (.in(xor_5_out));
  or or_20 (or_20_out, A2, B2);
  and and_29 (and_29_out, A1, B1);
  and and_30 (and_30_out, or_20_out, or_22_out);
  and and_31 (and_31_out, and_30_out, and_38_out);
  or or_21 (or_21_out, and_29_out, and_33_out);
  or or_22 (or_22_out, A1, B1);
  and and_32 (and_32_out, ~and_29_out, or_22_out);  // AND_Gate
  and and_33 (and_33_out, or_24_out, or_22_out);
  and and_34 (and_34_out, or_22_out, and_38_out);
  or or_23 (or_23_out, or_21_out, and_34_out);
  xor xor_6 (xor_6_out, and_26_out, or_23_out);
  LED led_6 (.in(xor_6_out));
  and and_35 (and_35_out, A0, B0);
  and and_36 (and_36_out, ~and_35_out, or_25_out);  // AND_Gate
  and and_37 (and_37_out, 1'b0, or_25_out);
  or or_24 (or_24_out, and_35_out, and_37_out);
  xor xor_7 (xor_7_out, and_32_out, or_26_out);
  LED led_7 (.in(xor_7_out));
  or or_25 (or_25_out, A0, B0);
  and and_38 (and_38_out, or_25_out, 1'b0);
  or or_26 (or_26_out, or_24_out, and_38_out);
  LED led_8 (.in(and_36_out));
  LED led_9 (.in(or_27_out));
  and and_39 (and_39_out, or_36_out, and_47_out);
  or or_27 (or_27_out, or_29_out, and_39_out);
  xor xor_8 (xor_8_out, or_31_out, and_41_out);
  LED led_10 (.in(xor_8_out));
  and and_40 (and_40_out, A6_2, B6_2);
  or or_28 (or_28_out, A6_2, B6_2);
  and and_41 (and_41_out, ~and_40_out, or_28_out);  // AND_Gate
  and and_42 (and_42_out, or_30_out, or_28_out);
  or or_29 (or_29_out, and_40_out, and_42_out);
  // AND_Gate and_43 has open pins: in0=and_47_out, in1=and_60_out, out=open
  and and_44 (and_44_out, A5_2, B5_2);
  and and_45 (and_45_out, ~and_44_out, or_32_out);  // AND_Gate
  and and_46 (and_46_out, and_51_out, or_32_out);
  or or_30 (or_30_out, and_44_out, and_46_out);
  and and_47 (and_47_out, or_28_out, and_49_out);
  and and_48 (and_48_out, or_36_out, and_49_out);
  or or_31 (or_31_out, or_30_out, and_48_out);
  xor xor_9 (xor_9_out, or_33_out, and_45_out);
  LED led_11 (.in(xor_9_out));
  or or_32 (or_32_out, A5_2, B5_2);
  and and_49 (and_49_out, or_32_out, or_34_out);
  // AND_Gate and_50 has open pins: in0=and_49_out, in1=and_60_out, out=open
  or or_33 (or_33_out, and_51_out, and_53_out);
  and and_51 (and_51_out, A4_2, B4_2);
  or or_34 (or_34_out, A4_2, B4_2);
  and and_52 (and_52_out, ~and_51_out, or_34_out);  // AND_Gate
  and and_53 (and_53_out, or_36_out, or_34_out);
  // AND_Gate and_54 has open pins: in0=or_34_out, in1=and_60_out, out=open
  xor xor_10 (xor_10_out, or_36_out, and_52_out);
  LED led_12 (.in(xor_10_out));
  and and_55 (and_55_out, A3_2, B3_2);
  and and_56 (and_56_out, ~and_55_out, or_37_out);  // AND_Gate
  and and_57 (and_57_out, and_61_out, or_37_out);
  or or_35 (or_35_out, and_55_out, and_57_out);
  and and_58 (and_58_out, or_40_out, and_59_out);
  or or_36 (or_36_out, or_35_out, and_58_out);
  xor xor_11 (xor_11_out, or_39_out, and_56_out);
  LED led_13 (.in(xor_11_out));
  or or_37 (or_37_out, A3_2, B3_2);
  and and_59 (and_59_out, or_37_out, or_38_out);
  and and_60 (and_60_out, and_59_out, and_68_out);
  and and_61 (and_61_out, A2_2, B2_2);
  or or_38 (or_38_out, A2_2, B2_2);
  and and_62 (and_62_out, ~and_61_out, or_38_out);  // AND_Gate
  and and_63 (and_63_out, or_40_out, or_38_out);
  or or_39 (or_39_out, and_61_out, and_63_out);
  xor xor_12 (xor_12_out, or_40_out, and_62_out);
  LED led_14 (.in(xor_12_out));
  and and_64 (and_64_out, A1_2, B1_2);
  and and_65 (and_65_out, ~and_64_out, or_41_out);  // AND_Gate
  and and_66 (and_66_out, and_69_out, or_41_out);
  or or_40 (or_40_out, and_64_out, and_66_out);
  // AND_Gate and_67 has open pins: in0=or_38_out, in1=and_68_out, out=open
  or or_41 (or_41_out, A1_2, B1_2);
  and and_68 (and_68_out, or_41_out, or_42_out);
  xor xor_13 (xor_13_out, and_69_out, and_65_out);
  LED led_15 (.in(xor_13_out));
  and and_69 (and_69_out, A0_2, B0_2);
  or or_42 (or_42_out, A0_2, B0_2);
  and and_70 (and_70_out, ~and_69_out, or_42_out);  // AND_Gate
  LED led_16 (.in(and_70_out));

  // Notes on the sheet:
  //   G6
  //   H6
  //   P6
  //   G5
  //   H5
  //   P5
  //   G4
  //   H4
  //   P4
  //   G3
  //   H3
  //   P3
  //   P2
  //   G2
  //   H2
  //   G1
  //   H1
  //   P1
  //   G0
  //   H0
  //   P0
endmodule
