// Logisim project LadnerFischerAdderModuloBasic.circ as structural Verilog: 1 circuit, main circuit main
module main (
  input  A6,
  input  A5,
  input  A4,
  input  A3,
  input  A2,
  input  A1,
  input  A0,
  input  A6_2,
  input  A5_2,
  input  A4_2,
  input  A3_2,
  input  A2_2,
  input  A1_2,
  input  A0_2,
  input  B6,
  input  B5,
  input  B4,
  input  B3,
  input  B2,
  input  B1,
  input  B0,
  input  B6_2,
  input  B5_2,
  input  B4_2,
  input  B3_2,
  input  B2_2,
  input  B1_2,
  input  B0_2
);

  wire and_1_out, and_2_out, and_3_out, and_4_out, and_5_out, and_6_out, and_7_out, and_8_out, and_9_out,
       and_10_out, and_11_out, and_12_out, and_13_out, and_14_out, and_15_out, and_16_out, and_17_out,
       and_18_out, and_19_out, and_20_out, and_21_out, and_22_out, and_23_out, and_24_out, and_25_out,
       and_26_out, and_27_out, and_28_out, and_29_out, and_30_out, and_31_out, and_32_out, and_33_out,
       and_34_out, and_35_out, and_36_out, and_37_out, and_38_out, and_39_out, and_40_out, and_41_out,
       and_42_out, and_43_out, and_44_out, and_45_out, and_46_out, and_47_out, and_48_out, and_49_out,
       and_50_out, and_51_out, and_52_out, and_53_out, and_54_out, and_55_out, and_56_out, and_57_out,
       and_58_out, and_59_out, and_60_out, and_61_out, and_62_out, and_63_out, and_64_out, and_65_out,
       and_66_out, and_67_out, and_68_out, and_69_out, and_70_out, and_71_out, and_72_out, and_73_out,
       and_74_out, and_75_out, and_76_out, and_77_out, and_78_out, and_79_out, and_80_out, and_81_out,
       and_82_out, and_83_out, and_84_out, and_85_out, and_86_out, and_87_out, and_88_out, and_89_out,
       and_90_out, and_91_out, and_92_out, and_93_out, and_94_out, and_95_out, and_96_out, and_97_out,
       and_98_out, and_99_out, and_100_out, and_101_out, and_102_out, and_103_out, and_104_out, and_105_out,
       and_106_out, and_107_out, and_108_out, and_109_out, and_110_out, and_111_out, and_112_out,
       and_113_out, and_114_out, and_115_out, and_116_out, and_117_out, and_118_out, and_119_out,
       and_120_out, and_121_out, and_122_out, and_123_out, and_124_out, and_125_out, and_126_out,
       and_127_out, and_128_out, and_129_out, and_130_out, and_131_out, and_132_out, and_133_out,
       and_134_out, and_135_out, and_136_out, and_137_out, and_138_out, and_139_out, and_140_out,
       multiplexer_1_out, multiplexer_2_out, multiplexer_3_out, multiplexer_4_out, multiplexer_5_out,
       multiplexer_6_out, multiplexer_7_out, multiplexer_8_out, multiplexer_9_out, multiplexer_10_out,
       multiplexer_11_out, multiplexer_12_out, multiplexer_13_out, multiplexer_14_out, multiplexer_15_out,
       multiplexer_16_out, multiplexer_17_out, multiplexer_18_out, multiplexer_19_out, multiplexer_20_out,
       multiplexer_21_out, multiplexer_22_out, multiplexer_23_out, multiplexer_24_out, multiplexer_25_out,
       multiplexer_26_out, nor_1_out, nor_2_out, not_5_out, not_7_out, not_12_out, not_14_out, or_1_out,
       or_2_out, or_3_out, or_4_out, or_5_out, or_6_out, or_7_out, or_8_out, or_9_out, or_10_out, or_11_out,
       or_12_out, or_13_out, or_14_out, or_15_out, or_16_out, or_17_out, or_18_out, or_19_out, or_20_out,
       or_21_out, or_22_out, or_23_out, or_24_out, or_25_out, or_26_out, or_27_out, or_28_out, or_29_out,
       or_30_out, or_31_out, or_32_out, or_33_out, or_34_out, or_35_out, or_36_out, or_37_out, or_38_out,
       or_39_out, or_40_out, or_41_out, or_42_out, or_43_out, or_44_out, or_45_out, or_46_out, or_47_out,
       or_48_out, or_49_out, or_50_out, or_51_out, or_52_out, or_53_out, or_54_out, or_55_out, or_56_out,
       or_57_out, or_58_out, or_59_out, or_60_out, or_61_out, or_62_out, or_63_out, or_64_out, or_65_out,
       or_66_out, or_67_out, or_68_out, or_69_out, or_70_out, or_71_out, or_72_out, or_73_out, or_74_out,
       or_75_out, or_76_out, or_77_out, or_78_out, or_79_out, or_80_out, or_81_out, or_82_out, or_83_out,
       or_84_out, xor_1_out, xor_2_out, xor_3_out, xor_4_out, xor_5_out, xor_6_out, xor_7_out, xor_8_out,
       xor_9_out, xor_10_out, xor_11_out, xor_12_out, xor_13_out, xor_14_out;

  nor nor_1 (nor_1_out, or_4_out, or_7_out);
  or or_1 (or_1_out, and_5_out, and_7_out);
  and and_1 (and_1_out, or_19_out, and_8_out);
  or or_2 (or_2_out, or_1_out, and_1_out);
  and and_2 (and_2_out, or_34_out, and_9_out);
  or or_3 (or_3_out, or_2_out, and_2_out);
  or or_4 (or_4_out, or_3_out, and_10_out);
  Multiplexer multiplexer_1 (.in0(and_6_out), .in1(and_4_out), .out(multiplexer_1_out), .sel(nor_1_out));
  and and_3 (and_3_out, A6, B6);
  and and_4 (and_4_out, ~and_3_out, or_8_out);  // AND_Gate
  and and_5 (and_5_out, and_4_out, and_19_out);
  and and_6 (and_6_out, ~and_5_out, or_9_out);  // AND_Gate
  and and_7 (and_7_out, and_21_out, or_9_out);
  and and_8 (and_8_out, or_9_out, or_14_out);
  and and_9 (and_9_out, and_8_out, and_35_out);
  or or_5 (or_5_out, or_10_out, and_13_out);
  and and_10 (and_10_out, and_9_out, and_56_out);
  and and_11 (and_11_out, or_36_out, and_14_out);
  or or_6 (or_6_out, or_5_out, and_11_out);
  or or_7 (or_7_out, or_6_out, and_15_out);
  Multiplexer multiplexer_2 (.in0(or_13_out), .in1(or_17_out), .out(multiplexer_2_out), .sel(nor_1_out));
  xor xor_1 (xor_1_out, multiplexer_1_out, multiplexer_2_out);
  or or_8 (or_8_out, A6, B6);
  // NOT_Gate not_1 has open pins: in=and_4_out, out=open
  or or_9 (or_9_out, and_4_out, and_19_out);
  and and_12 (and_12_out, and_19_out, or_8_out);
  or or_10 (or_10_out, and_3_out, and_12_out);
  and and_13 (and_13_out, or_24_out, and_16_out);
  and and_14 (and_14_out, and_16_out, and_39_out);
  and and_15 (and_15_out, and_14_out, and_59_out);
  and and_16 (and_16_out, or_8_out, or_18_out);
  and and_17 (and_17_out, or_19_out, or_14_out);
  or or_11 (or_11_out, and_21_out, and_17_out);
  and and_18 (and_18_out, or_34_out, and_23_out);
  or or_12 (or_12_out, or_11_out, and_18_out);
  or or_13 (or_13_out, or_12_out, and_24_out);
  Multiplexer multiplexer_3 (.in0(and_22_out), .in1(and_20_out), .out(multiplexer_3_out), .sel(nor_1_out));
  and and_19 (and_19_out, A5, B5);
  and and_20 (and_20_out, ~and_19_out, or_18_out);  // AND_Gate
  // NOT_Gate not_2 has open pins: in=and_20_out, out=open
  and and_21 (and_21_out, and_20_out, and_32_out);
  or or_14 (or_14_out, and_20_out, and_32_out);
  and and_22 (and_22_out, ~and_21_out, or_14_out);  // AND_Gate
  and and_23 (and_23_out, or_14_out, and_35_out);
  or or_15 (or_15_out, and_19_out, and_26_out);
  and and_24 (and_24_out, and_23_out, and_56_out);
  and and_25 (and_25_out, or_36_out, and_27_out);
  or or_16 (or_16_out, or_15_out, and_25_out);
  or or_17 (or_17_out, or_16_out, and_28_out);
  Multiplexer multiplexer_4 (.in0(or_21_out), .in1(or_26_out), .out(multiplexer_4_out), .sel(nor_1_out));
  xor xor_2 (xor_2_out, multiplexer_3_out, multiplexer_4_out);
  or or_18 (or_18_out, A5, B5);
  and and_26 (and_26_out, or_24_out, or_18_out);
  and and_27 (and_27_out, or_18_out, and_39_out);
  and and_28 (and_28_out, and_27_out, and_59_out);
  and and_29 (and_29_out, and_33_out, and_41_out);
  and and_30 (and_30_out, and_42_out, or_23_out);
  or or_19 (or_19_out, and_29_out, and_30_out);
  and and_31 (and_31_out, or_34_out, and_35_out);
  or or_20 (or_20_out, or_19_out, and_31_out);
  or or_21 (or_21_out, or_20_out, and_37_out);
  Multiplexer multiplexer_5 (.in0(and_34_out), .in1(and_33_out), .out(multiplexer_5_out), .sel(nor_1_out));
  or or_22 (or_22_out, A4, B4);
  and and_32 (and_32_out, A4, B4);
  and and_33 (and_33_out, ~and_32_out, or_22_out);  // AND_Gate
  // NOT_Gate not_3 has open pins: in=and_33_out, out=open
  or or_23 (or_23_out, and_33_out, and_41_out);
  and and_34 (and_34_out, ~and_29_out, or_23_out);  // AND_Gate
  and and_35 (and_35_out, or_23_out, or_30_out);
  and and_36 (and_36_out, and_41_out, or_22_out);
  or or_24 (or_24_out, and_32_out, and_36_out);
  and and_37 (and_37_out, and_35_out, and_56_out);
  and and_38 (and_38_out, or_36_out, and_39_out);
  or or_25 (or_25_out, or_24_out, and_38_out);
  or or_26 (or_26_out, or_25_out, and_40_out);
  Multiplexer multiplexer_6 (.in0(or_28_out), .in1(or_32_out), .out(multiplexer_6_out), .sel(nor_1_out));
  xor xor_3 (xor_3_out, multiplexer_5_out, multiplexer_6_out);
  and and_39 (and_39_out, or_22_out, or_29_out);
  and and_40 (and_40_out, and_39_out, and_59_out);
  and and_41 (and_41_out, A3, B3);
  and and_42 (and_42_out, and_44_out, or_37_out);
  and and_43 (and_43_out, or_34_out, or_30_out);
  or or_27 (or_27_out, and_42_out, and_43_out);
  or or_28 (or_28_out, or_27_out, and_46_out);
  Multiplexer multiplexer_7 (.in0(and_45_out), .in1(and_44_out), .out(multiplexer_7_out), .sel(nor_1_out));
  or or_29 (or_29_out, A3, B3);
  and and_44 (and_44_out, ~and_41_out, or_29_out);  // AND_Gate
  // NOT_Gate not_4 has open pins: in=and_44_out, out=open
  or or_30 (or_30_out, and_44_out, or_37_out);
  and and_45 (and_45_out, ~and_42_out, or_30_out);  // AND_Gate
  and and_46 (and_46_out, or_30_out, and_56_out);
  and and_47 (and_47_out, or_36_out, or_29_out);
  or or_31 (or_31_out, and_41_out, and_47_out);
  or or_32 (or_32_out, or_31_out, and_48_out);
  Multiplexer multiplexer_8 (.in0(or_35_out), .in1(or_40_out), .out(multiplexer_8_out), .sel(nor_1_out));
  xor xor_4 (xor_4_out, multiplexer_7_out, multiplexer_8_out);
  and and_48 (and_48_out, or_29_out, and_59_out);
  or or_33 (or_33_out, and_52_out, and_54_out);
  and and_49 (and_49_out, or_47_out, and_55_out);
  or or_34 (or_34_out, or_33_out, and_49_out);
  or or_35 (or_35_out, or_34_out, and_56_out);
  and and_50 (and_50_out, A2, B2);
  and and_51 (and_51_out, ~and_50_out, or_37_out);  // AND_Gate
  and and_52 (and_52_out, not_5_out, and_62_out);
  and and_53 (and_53_out, ~and_52_out, or_38_out);  // AND_Gate
  and and_54 (and_54_out, and_64_out, or_38_out);
  and and_55 (and_55_out, or_38_out, or_43_out);
  and and_56 (and_56_out, and_55_out, and_74_out);
  or or_36 (or_36_out, or_39_out, and_58_out);
  Multiplexer multiplexer_9 (.in0(and_53_out), .in1(and_51_out), .out(multiplexer_9_out), .sel(nor_1_out));
  Multiplexer multiplexer_10 (.in0(or_42_out), .in1(or_46_out), .out(multiplexer_10_out), .sel(nor_1_out));
  xor xor_5 (xor_5_out, multiplexer_9_out, multiplexer_10_out);
  or or_37 (or_37_out, A2, B2);
  not not_5 (not_5_out, and_51_out);
  or or_38 (or_38_out, not_5_out, and_62_out);
  and and_57 (and_57_out, and_62_out, or_37_out);
  or or_39 (or_39_out, and_50_out, and_57_out);
  and and_58 (and_58_out, or_51_out, and_60_out);
  and and_59 (and_59_out, and_60_out, and_76_out);
  or or_40 (or_40_out, or_36_out, and_59_out);
  and and_60 (and_60_out, or_37_out, or_45_out);
  and and_61 (and_61_out, or_47_out, or_43_out);
  or or_41 (or_41_out, and_64_out, and_61_out);
  or or_42 (or_42_out, or_41_out, and_66_out);
  and and_62 (and_62_out, A1, B1);
  and and_63 (and_63_out, ~and_62_out, or_45_out);  // AND_Gate
  // NOT_Gate not_6 has open pins: in=and_63_out, out=open
  and and_64 (and_64_out, and_63_out, or_49_out);
  or or_43 (or_43_out, and_63_out, or_49_out);
  and and_65 (and_65_out, ~and_64_out, or_43_out);  // AND_Gate
  and and_66 (and_66_out, or_43_out, and_74_out);
  or or_44 (or_44_out, and_62_out, and_67_out);
  Multiplexer multiplexer_11 (.in0(and_65_out), .in1(and_63_out), .out(multiplexer_11_out), .sel(nor_1_out));
  Multiplexer multiplexer_12 (.in0(or_48_out), .in1(or_52_out), .out(multiplexer_12_out), .sel(nor_1_out));
  xor xor_6 (xor_6_out, multiplexer_11_out, multiplexer_12_out);
  or or_45 (or_45_out, A1, B1);
  and and_67 (and_67_out, or_51_out, or_45_out);
  and and_68 (and_68_out, or_45_out, and_76_out);
  or or_46 (or_46_out, or_44_out, and_68_out);
  and and_69 (and_69_out, 1'b0, or_50_out);
  or or_47 (or_47_out, and_72_out, and_69_out);
  or or_48 (or_48_out, or_47_out, and_74_out);
  and and_70 (and_70_out, A0, B0);
  or or_49 (or_49_out, A0, B0);
  and and_71 (and_71_out, ~and_70_out, or_49_out);  // AND_Gate
  not not_7 (not_7_out, and_71_out);
  and and_72 (and_72_out, not_7_out, 1'b0);
  or or_50 (or_50_out, not_7_out, 1'b0);
  and and_73 (and_73_out, ~and_72_out, or_50_out);  // AND_Gate
  and and_74 (and_74_out, or_50_out, 1'b0);
  and and_75 (and_75_out, 1'b0, or_49_out);
  or or_51 (or_51_out, and_70_out, and_75_out);
  or or_52 (or_52_out, or_51_out, and_76_out);
  Multiplexer multiplexer_13 (.in0(and_73_out), .in1(and_71_out), .out(multiplexer_13_out), .sel(nor_1_out));
  xor xor_7 (xor_7_out, multiplexer_13_out, 1'b0);
  and and_76 (and_76_out, or_49_out, 1'b0);
  LED led_1 (.in(xor_1_out));
  LED led_2 (.in(xor_2_out));
  LED led_3 (.in(xor_3_out));
  LED led_4 (.in(xor_4_out));
  LED led_5 (.in(xor_5_out));
  LED led_6 (.in(xor_6_out));
  LED led_7 (.in(xor_7_out));
  nor nor_2 (nor_2_out, or_54_out, or_56_out);
  or or_53 (or_53_out, and_80_out, and_82_out);
  and and_77 (and_77_out, or_69_out, and_83_out);
  or or_54 (or_54_out, or_53_out, and_77_out);
  Multiplexer multiplexer_14 (.in0(and_81_out), .in1(and_79_out), .out(multiplexer_14_out), .sel(nor_2_out));
  and and_78 (and_78_out, A6_2, B6_2);
  and and_79 (and_79_out, ~and_78_out, or_57_out);  // AND_Gate
  // NOT_Gate not_8 has open pins: in=and_79_out, out=open
  and and_80 (and_80_out, and_79_out, and_91_out);
  and and_81 (and_81_out, ~and_80_out, or_58_out);  // AND_Gate
  and and_82 (and_82_out, or_59_out, or_58_out);
  and and_83 (and_83_out, or_58_out, and_95_out);
  or or_55 (or_55_out, and_78_out, and_86_out);
  and and_84 (and_84_out, and_83_out, and_114_out);
  and and_85 (and_85_out, or_71_out, and_87_out);
  or or_56 (or_56_out, or_55_out, and_85_out);
  Multiplexer multiplexer_15 (.in0(or_60_out), .in1(or_64_out), .out(multiplexer_15_out), .sel(nor_2_out));
  xor xor_8 (xor_8_out, multiplexer_14_out, multiplexer_15_out);
  or or_57 (or_57_out, A6_2, B6_2);
  or or_58 (or_58_out, and_79_out, and_91_out);
  and and_86 (and_86_out, or_63_out, or_57_out);
  and and_87 (and_87_out, or_57_out, and_99_out);
  and and_88 (and_88_out, and_87_out, and_119_out);
  and and_89 (and_89_out, and_102_out, or_62_out);
  or or_59 (or_59_out, and_93_out, and_89_out);
  and and_90 (and_90_out, or_69_out, and_95_out);
  or or_60 (or_60_out, or_59_out, and_90_out);
  Multiplexer multiplexer_16 (.in0(and_94_out), .in1(and_92_out), .out(multiplexer_16_out), .sel(nor_2_out));
  and and_91 (and_91_out, A5_2, B5_2);
  or or_61 (or_61_out, A5_2, B5_2);
  and and_92 (and_92_out, ~and_91_out, or_61_out);  // AND_Gate
  // NOT_Gate not_9 has open pins: in=and_92_out, out=open
  and and_93 (and_93_out, and_92_out, and_101_out);
  or or_62 (or_62_out, and_92_out, and_101_out);
  and and_94 (and_94_out, ~and_93_out, or_62_out);  // AND_Gate
  and and_95 (and_95_out, or_62_out, or_67_out);
  and and_96 (and_96_out, and_101_out, or_61_out);
  or or_63 (or_63_out, and_91_out, and_96_out);
  and and_97 (and_97_out, and_95_out, and_114_out);
  and and_98 (and_98_out, or_71_out, and_99_out);
  or or_64 (or_64_out, or_63_out, and_98_out);
  Multiplexer multiplexer_17 (.in0(or_65_out), .in1(or_68_out), .out(multiplexer_17_out), .sel(nor_2_out));
  xor xor_9 (xor_9_out, multiplexer_16_out, multiplexer_17_out);
  and and_99 (and_99_out, or_61_out, or_66_out);
  and and_100 (and_100_out, and_99_out, and_119_out);
  and and_101 (and_101_out, A4_2, B4_2);
  and and_102 (and_102_out, and_104_out, and_109_out);
  and and_103 (and_103_out, or_69_out, or_67_out);
  or or_65 (or_65_out, and_102_out, and_103_out);
  Multiplexer multiplexer_18 (.in0(and_105_out), .in1(and_104_out), .out(multiplexer_18_out), .sel(nor_2_out));
  xor xor_10 (xor_10_out, multiplexer_18_out, multiplexer_19_out);
  or or_66 (or_66_out, A4_2, B4_2);
  and and_104 (and_104_out, ~and_101_out, or_66_out);  // AND_Gate
  // NOT_Gate not_10 has open pins: in=and_104_out, out=open
  or or_67 (or_67_out, and_104_out, and_109_out);
  and and_105 (and_105_out, ~and_102_out, or_67_out);  // AND_Gate
  and and_106 (and_106_out, or_67_out, and_114_out);
  and and_107 (and_107_out, or_71_out, or_66_out);
  or or_68 (or_68_out, and_101_out, and_107_out);
  Multiplexer multiplexer_19 (.in0(or_69_out), .in1(or_71_out), .out(multiplexer_19_out), .sel(nor_2_out));
  and and_108 (and_108_out, or_66_out, and_119_out);
  or or_69 (or_69_out, or_70_out, and_113_out);
  and and_109 (and_109_out, A3_2, B3_2);
  and and_110 (and_110_out, and_115_out, or_77_out);
  and and_111 (and_111_out, ~and_110_out, or_73_out);  // AND_Gate
  and and_112 (and_112_out, and_123_out, or_73_out);
  or or_70 (or_70_out, and_110_out, and_112_out);
  and and_113 (and_113_out, or_79_out, and_116_out);
  and and_114 (and_114_out, and_116_out, and_134_out);
  or or_71 (or_71_out, or_74_out, and_118_out);
  Multiplexer multiplexer_20 (.in0(and_111_out), .in1(and_115_out), .out(multiplexer_20_out), .sel(nor_2_out));
  xor xor_11 (xor_11_out, multiplexer_20_out, multiplexer_21_out);
  or or_72 (or_72_out, A3_2, B3_2);
  and and_115 (and_115_out, ~and_109_out, or_72_out);  // AND_Gate
  // NOT_Gate not_11 has open pins: in=and_115_out, out=open
  or or_73 (or_73_out, and_115_out, or_77_out);
  and and_116 (and_116_out, or_73_out, or_78_out);
  and and_117 (and_117_out, and_121_out, or_72_out);
  or or_74 (or_74_out, and_109_out, and_117_out);
  and and_118 (and_118_out, or_82_out, and_120_out);
  and and_119 (and_119_out, and_120_out, and_136_out);
  Multiplexer multiplexer_21 (.in0(or_75_out), .in1(or_76_out), .out(multiplexer_21_out), .sel(nor_2_out));
  and and_120 (and_120_out, or_72_out, or_77_out);
  or or_75 (or_75_out, and_123_out, and_125_out);
  and and_121 (and_121_out, A2_2, B2_2);
  and and_122 (and_122_out, ~and_121_out, or_77_out);  // AND_Gate
  not not_12 (not_12_out, and_122_out);
  and and_123 (and_123_out, not_12_out, and_130_out);
  and and_124 (and_124_out, ~and_123_out, or_78_out);  // AND_Gate
  and and_125 (and_125_out, or_79_out, or_78_out);
  and and_126 (and_126_out, or_78_out, and_134_out);
  or or_76 (or_76_out, and_121_out, and_127_out);
  Multiplexer multiplexer_22 (.in0(and_124_out), .in1(and_122_out), .out(multiplexer_22_out), .sel(nor_2_out));
  Multiplexer multiplexer_23 (.in0(or_79_out), .in1(or_82_out), .out(multiplexer_23_out), .sel(nor_2_out));
  xor xor_12 (xor_12_out, multiplexer_22_out, multiplexer_23_out);
  or or_77 (or_77_out, A2_2, B2_2);
  or or_78 (or_78_out, not_12_out, and_130_out);
  and and_127 (and_127_out, or_82_out, or_77_out);
  and and_128 (and_128_out, or_77_out, and_136_out);
  and and_129 (and_129_out, and_138_out, or_81_out);
  or or_79 (or_79_out, and_132_out, and_129_out);
  and and_130 (and_130_out, A1_2, B1_2);
  or or_80 (or_80_out, A1_2, B1_2);
  and and_131 (and_131_out, ~and_130_out, or_80_out);  // AND_Gate
  // NOT_Gate not_13 has open pins: in=and_131_out, out=open
  and and_132 (and_132_out, and_131_out, or_83_out);
  or or_81 (or_81_out, and_131_out, or_83_out);
  and and_133 (and_133_out, ~and_132_out, or_81_out);  // AND_Gate
  and and_134 (and_134_out, or_81_out, or_84_out);
  and and_135 (and_135_out, and_137_out, or_80_out);
  or or_82 (or_82_out, and_130_out, and_135_out);
  Multiplexer multiplexer_24 (.in0(and_133_out), .in1(and_131_out), .out(multiplexer_24_out), .sel(nor_2_out));
  Multiplexer multiplexer_25 (.in0(and_138_out), .in1(and_137_out), .out(multiplexer_25_out), .sel(nor_2_out));
  xor xor_13 (xor_13_out, multiplexer_24_out, multiplexer_25_out);
  and and_136 (and_136_out, or_80_out, or_83_out);
  and and_137 (and_137_out, A0_2, B0_2);
  and and_138 (and_138_out, not_14_out, 1'b0);
  Multiplexer multiplexer_26 (.in0(and_140_out), .in1(and_139_out), .out(multiplexer_26_out), .sel(nor_2_out));
  or or_83 (or_83_out, A0_2, B0_2);
  and and_139 (and_139_out, ~and_137_out, or_83_out);  // AND_Gate
  not not_14 (not_14_out, and_139_out);
  or or_84 (or_84_out, not_14_out, 1'b0);
  and and_140 (and_140_out, ~and_138_out, or_84_out);  // AND_Gate
  xor xor_14 (xor_14_out, multiplexer_26_out, 1'b0);
  LED led_8 (.in(xor_8_out));
  LED led_9 (.in(xor_9_out));
  LED led_10 (.in(xor_10_out));
  LED led_11 (.in(xor_11_out));
  LED led_12 (.in(xor_12_out));
  LED led_13 (.in(xor_13_out));
  LED led_14 (.in(xor_14_out));

  // Notes on the sheet:
  //   C'OUT
  //   COUT
  //   H'
  //   H
  //   G6
  //   H6
  //   G'6
  //   H'6
  //   P'6
  //   P6
  //   G'5
  //   G5
  //   H5
  //   P5
  //   H'5
  //   P'5
  //   G4
  //   G'4
  //   P4
  //   H4
  //   H'4
  //   P'4
  //   G3
  //   H3
  //   G'3
  //   H'3
  //   P3
  //   P'3
  //   G2
  //   H2
  //   G'2
  //   H'2
  //   P'2
  //   P2
  //   G'1
  //   G1
  //   H1
  //   P1
  //   H'1
  //   P'1
  //   G0
  //   G'0
  //   H0
  //   P0
  //   H'0
  //   P'0
  //   C'OUT
  //   H'
  //   H
  //   P6
  //   G6
  //   H6
  //   G'6
  //   H'6
  //   P'6
  //   G5
  //   G'5
  //   H5
  //   P5
  //   H'5
  //   P'5
  //   G4
  //   G'4
  //   H'4
  //   H4
  //   P4
  //   P'4
  //   G3
  //   H3
  //   G'3
  //   H'3
  //   P3
  //   P'3
  //   G2
  //   H2
  //   P2
  //   G'2
  //   H'2
  //   P'2
  //   G1
  //   G'1
  //   H1
  //   P1
  //   H'1
  //   P'1
  //   G0
  //   G'0
  //   H0
  //   P0
  //   H'0
  //   P'0
endmodule
