// Logisim project LadnerFischerAdderModuloOptimised.circ as structural Verilog: 1 circuit, main circuit main
module main (
  input  A6,
  input  A5,
  input  A4,
  input  A3,
  input  A2,
  input  A1,
  input  A0,
  input  B6,
  input  B5,
  input  B4,
  input  B3,
  input  B2,
  input  B1,
  input  B0
);

  wire and_1_out, and_2_out, and_3_out, and_4_out, and_5_out, and_6_out, and_7_out, and_8_out, and_9_out,
       and_10_out, and_11_out, and_12_out, and_13_out, and_14_out, and_15_out, and_16_out, and_17_out,
       and_18_out, and_19_out, and_20_out, and_21_out, and_22_out, and_23_out, and_24_out, and_25_out,
       and_26_out, and_27_out, and_28_out, and_29_out, and_30_out, and_31_out, and_32_out, and_33_out,
       and_34_out, and_35_out, and_36_out, and_37_out, and_38_out, and_39_out, and_40_out, and_41_out,
       and_42_out, and_43_out, and_44_out, and_45_out, and_46_out, and_47_out, and_48_out, and_49_out,
       and_50_out, and_51_out, and_52_out, multiplexer_1_out, multiplexer_2_out, multiplexer_3_out,
       multiplexer_4_out, multiplexer_5_out, multiplexer_6_out, multiplexer_7_out, multiplexer_8_out,
       multiplexer_9_out, multiplexer_10_out, multiplexer_11_out, multiplexer_12_out, multiplexer_13_out,
       nor_1_out, not_5_out, not_7_out, or_1_out, or_2_out, or_3_out, or_4_out, or_5_out, or_6_out, or_7_out,
       or_8_out, or_9_out, or_10_out, or_11_out, or_12_out, or_13_out, or_14_out, or_15_out, or_16_out,
       or_17_out, or_18_out, or_19_out, or_20_out, or_21_out, or_22_out, or_23_out, or_24_out, or_25_out,
       or_26_out, or_27_out, or_28_out, or_29_out, or_30_out, or_31_out, or_32_out, xor_1_out, xor_2_out,
       xor_3_out, xor_4_out, xor_5_out, xor_6_out, xor_7_out;

  nor nor_1 (nor_1_out, or_2_out, or_3_out);
  or or_1 (or_1_out, and_4_out, and_6_out);
  and and_1 (and_1_out, or_17_out, and_7_out);
  or or_2 (or_2_out, or_1_out, and_1_out);
  Multiplexer multiplexer_1 (.in0(and_5_out), .in1(and_3_out), .out(multiplexer_1_out), .sel(nor_1_out));
  and and_2 (and_2_out, A6, B6);
  and and_3 (and_3_out, ~and_2_out, or_4_out);  // AND_Gate
  and and_4 (and_4_out, and_3_out, and_13_out);
  and and_5 (and_5_out, ~and_4_out, or_5_out);  // AND_Gate
  and and_6 (and_6_out, or_7_out, or_5_out);
  and and_7 (and_7_out, or_5_out, and_17_out);
  or or_3 (or_3_out, or_6_out, and_9_out);
  Multiplexer multiplexer_2 (.in0(or_8_out), .in1(or_11_out), .out(multiplexer_2_out), .sel(nor_1_out));
  xor xor_1 (xor_1_out, multiplexer_1_out, multiplexer_2_out);
  or or_4 (or_4_out, A6, B6);
  // NOT_Gate not_1 has open pins: in=and_3_out, out=open
  or or_5 (or_5_out, and_3_out, and_13_out);
  and and_8 (and_8_out, or_10_out, or_4_out);
  or or_6 (or_6_out, and_2_out, and_8_out);
  and and_9 (and_9_out, or_22_out, and_10_out);
  and and_10 (and_10_out, or_4_out, and_20_out);
  and and_11 (and_11_out, and_21_out, or_9_out);
  or or_7 (or_7_out, and_15_out, and_11_out);
  and and_12 (and_12_out, or_17_out, and_17_out);
  or or_8 (or_8_out, or_7_out, and_12_out);
  Multiplexer multiplexer_3 (.in0(and_16_out), .in1(and_14_out), .out(multiplexer_3_out), .sel(nor_1_out));
  and and_13 (and_13_out, A5, B5);
  and and_14 (and_14_out, ~and_13_out, or_12_out);  // AND_Gate
  // NOT_Gate not_2 has open pins: in=and_14_out, out=open
  and and_15 (and_15_out, and_14_out, and_23_out);
  or or_9 (or_9_out, and_14_out, and_23_out);
  and and_16 (and_16_out, ~and_15_out, or_9_out);  // AND_Gate
  and and_17 (and_17_out, or_9_out, or_15_out);
  or or_10 (or_10_out, and_13_out, and_19_out);
  and and_18 (and_18_out, or_22_out, and_20_out);
  or or_11 (or_11_out, or_10_out, and_18_out);
  Multiplexer multiplexer_4 (.in0(or_13_out), .in1(or_16_out), .out(multiplexer_4_out), .sel(nor_1_out));
  xor xor_2 (xor_2_out, multiplexer_3_out, multiplexer_4_out);
  or or_12 (or_12_out, A5, B5);
  and and_19 (and_19_out, and_23_out, or_12_out);
  and and_20 (and_20_out, or_12_out, or_14_out);
  and and_21 (and_21_out, and_24_out, and_27_out);
  and and_22 (and_22_out, or_17_out, or_15_out);
  or or_13 (or_13_out, and_21_out, and_22_out);
  Multiplexer multiplexer_5 (.in0(and_25_out), .in1(and_24_out), .out(multiplexer_5_out), .sel(nor_1_out));
  and and_23 (and_23_out, A4, B4);
  or or_14 (or_14_out, A4, B4);
  and and_24 (and_24_out, ~and_23_out, or_14_out);  // AND_Gate
  // NOT_Gate not_3 has open pins: in=and_24_out, out=open
  or or_15 (or_15_out, and_24_out, and_27_out);
  and and_25 (and_25_out, ~and_21_out, or_15_out);  // AND_Gate
  and and_26 (and_26_out, or_22_out, or_14_out);
  or or_16 (or_16_out, and_23_out, and_26_out);
  Multiplexer multiplexer_6 (.in0(or_17_out), .in1(or_22_out), .out(multiplexer_6_out), .sel(nor_1_out));
  xor xor_3 (xor_3_out, multiplexer_5_out, multiplexer_6_out);
  or or_17 (or_17_out, or_18_out, and_30_out);
  and and_27 (and_27_out, A3, B3);
  and and_28 (and_28_out, and_31_out, or_24_out);
  and and_29 (and_29_out, and_39_out, or_20_out);
  or or_18 (or_18_out, and_28_out, and_29_out);
  and and_30 (and_30_out, or_27_out, and_33_out);
  Multiplexer multiplexer_7 (.in0(and_32_out), .in1(and_31_out), .out(multiplexer_7_out), .sel(nor_1_out));
  or or_19 (or_19_out, A3, B3);
  and and_31 (and_31_out, ~and_27_out, or_19_out);  // AND_Gate
  // NOT_Gate not_4 has open pins: in=and_31_out, out=open
  or or_20 (or_20_out, and_31_out, or_24_out);
  and and_32 (and_32_out, ~and_28_out, or_20_out);  // AND_Gate
  and and_33 (and_33_out, or_20_out, or_25_out);
  and and_34 (and_34_out, and_37_out, or_19_out);
  or or_21 (or_21_out, and_27_out, and_34_out);
  and and_35 (and_35_out, or_29_out, and_36_out);
  or or_22 (or_22_out, or_21_out, and_35_out);
  Multiplexer multiplexer_8 (.in0(or_23_out), .in1(or_26_out), .out(multiplexer_8_out), .sel(nor_1_out));
  xor xor_4 (xor_4_out, multiplexer_7_out, multiplexer_8_out);
  and and_36 (and_36_out, or_19_out, or_24_out);
  or or_23 (or_23_out, and_39_out, and_41_out);
  and and_37 (and_37_out, A2, B2);
  and and_38 (and_38_out, ~and_37_out, or_24_out);  // AND_Gate
  and and_39 (and_39_out, not_5_out, and_44_out);
  and and_40 (and_40_out, ~and_39_out, or_25_out);  // AND_Gate
  and and_41 (and_41_out, or_27_out, or_25_out);
  Multiplexer multiplexer_9 (.in0(and_40_out), .in1(and_38_out), .out(multiplexer_9_out), .sel(nor_1_out));
  Multiplexer multiplexer_10 (.in0(or_27_out), .in1(or_29_out), .out(multiplexer_10_out), .sel(nor_1_out));
  xor xor_5 (xor_5_out, multiplexer_9_out, multiplexer_10_out);
  or or_24 (or_24_out, A2, B2);
  not not_5 (not_5_out, and_38_out);
  or or_25 (or_25_out, not_5_out, and_44_out);
  and and_42 (and_42_out, or_29_out, or_24_out);
  or or_26 (or_26_out, and_37_out, and_42_out);
  and and_43 (and_43_out, and_51_out, or_28_out);
  or or_27 (or_27_out, and_46_out, and_43_out);
  and and_44 (and_44_out, A1, B1);
  and and_45 (and_45_out, ~and_44_out, or_30_out);  // AND_Gate
  // NOT_Gate not_6 has open pins: in=and_45_out, out=open
  and and_46 (and_46_out, and_45_out, or_31_out);
  or or_28 (or_28_out, and_45_out, or_31_out);
  and and_47 (and_47_out, ~and_46_out, or_28_out);  // AND_Gate
  or or_29 (or_29_out, and_44_out, and_48_out);
  Multiplexer multiplexer_11 (.in0(and_47_out), .in1(and_45_out), .out(multiplexer_11_out), .sel(nor_1_out));
  Multiplexer multiplexer_12 (.in0(and_51_out), .in1(and_49_out), .out(multiplexer_12_out), .sel(nor_1_out));
  xor xor_6 (xor_6_out, multiplexer_11_out, multiplexer_12_out);
  or or_30 (or_30_out, A1, B1);
  and and_48 (and_48_out, and_49_out, or_30_out);
  and and_49 (and_49_out, A0, B0);
  or or_31 (or_31_out, A0, B0);
  and and_50 (and_50_out, ~and_49_out, or_31_out);  // AND_Gate
  not not_7 (not_7_out, and_50_out);
  and and_51 (and_51_out, not_7_out, 1'b0);
  or or_32 (or_32_out, not_7_out, 1'b0);
  and and_52 (and_52_out, ~and_51_out, or_32_out);  // AND_Gate
  Multiplexer multiplexer_13 (.in0(and_52_out), .in1(and_50_out), .out(multiplexer_13_out), .sel(nor_1_out));
  xor xor_7 (xor_7_out, multiplexer_13_out, 1'b0);
  LED led_1 (.in(xor_1_out));
  LED led_2 (.in(xor_2_out));
  LED led_3 (.in(xor_3_out));
  LED led_4 (.in(xor_4_out));
  LED led_5 (.in(xor_5_out));
  LED led_6 (.in(xor_6_out));
  LED led_7 (.in(xor_7_out));

  // Notes on the sheet:
  //   C'OUT
  //   H'
  //   H
  //   G6
  //   H6
  //   G'6
  //   H'6
  //   P'6
  //   P6
  //   G'5
  //   G5
  //   H5
  //   P5
  //   H'5
  //   P'5
  //   G4
  //   G'4
  //   H4
  //   P4
  //   H'4
  //   P'4
  //   G3
  //   H3
  //   G'3
  //   H'3
  //   P3
  //   P'3
  //   G2
  //   H2
  //   G'2
  //   H'2
  //   P'2
  //   P2
  //   G'1
  //   G1
  //   H1
  //   P1
  //   H'1
  //   P'1
  //   G0
  //   G'0
  //   H0
  //   P0
  //   H'0
  //   P'0
endmodule
